# Fritzing sketch schema (saved by Fritzing 1.0.1rc)
breadboards: 1

parts:
  U1 = ESP8266 NodeMCU LoLin module
  LED1 = DUO LED RG [package="5 mm [THT]"]
  SG1 = Buzzer 12mm [package=buzzer-ccv]

nets:
  N1: U1.D1, LED1.red_anode
  N2: U1.D2, LED1.green_anode
  N3: U1.GND, LED1.common_cathode, SG1.2
  N4: U1.D5, SG1.1

custom parts:
  ESP8266 NodeMCU LoLin module: ESP8266 based NodeMCU
